# Fritzing sketch BoardLayout (saved by Fritzing 0.9.4)
breadboards: 1
perfboards: 1

parts:
  M1 = STM32F103C8T6 blue mini board
  J2 = Dagu DGServo 9g header (male) [package=THT]
  J3 = Dagu DGServo 9g header (male) [package=THT]
  J4 = Dagu DGServo 9g header (male) [package=THT]
  J5 = Dagu DGServo 9g header (male) [package=THT]
  J6 = Dagu DGServo 9g header (male) [package=THT]
  J7 = Dagu DGServo 9g header (male) [package=THT]
  J8 = Dagu DGServo 9g header (male) [package=THT]
  J9 = Dagu DGServo 9g header (male) [package=THT]
  J10 = Dagu DGServo 9g header (male) [package=THT]
  J11 = Dagu DGServo 9g header (male) [package=THT]
  J12 = Dagu DGServo 9g header (male) [package=THT]
  J13 = Dagu DGServo 9g header (male) [package=THT]
  J14 = Dagu DGServo 9g header (male) [package=THT]
  J15 = Dagu DGServo 9g header (male) [package=THT]
  J16 = Dagu DGServo 9g header (male) [package=THT]
  5_volt_supply = Power plug
  J17 = Dagu DGServo 9g header (male) [package=THT]
  J18 = Dagu DGServo 9g header (male) [package=THT]
  J19 = Dagu DGServo 9g header (male) [package=THT]
  J20 = Dagu DGServo 9g header (male) [package=THT]
  J21 = Dagu DGServo 9g header (male) [package=THT]
  J22 = Dagu DGServo 9g header (male) [package=THT]
  J23 = Dagu DGServo 9g header (male) [package=THT]
  J24 = Dagu DGServo 9g header (male) [package=THT]
  J25 = Dagu DGServo 9g header (male) [package=THT]
  J26 = Dagu DGServo 9g header (male) [package=THT]
  J27 = Dagu DGServo 9g header (male) [package=THT]
  J28 = Dagu DGServo 9g header (male) [package=THT]
  J29 = Dagu DGServo 9g header (male) [package=THT]
  J30 = Dagu DGServo 9g header (male) [package=THT]
  J31 = Dagu DGServo 9g header (male) [package=THT]
  MIDI_Breakout = male pin header, 4 pins [form="♂ (male)"]
  Wafer_Servo = Dagu DGServo 9g header (male) [package=THT]

nets:
  N1: M1.B12, J22.pulse
  N2: M1.B13, J26.pulse
  N3: M1.B14, J25.pulse
  N4: M1.B15, J27.pulse
  N5: M1.A8, J30.pulse
  N6: M1.A9, MIDI_Breakout.pin4
  N7: M1.A10, MIDI_Breakout.pin3
  N8: M1.A11, J17.pulse
  N9: M1.A12, J18.pulse
  N10: M1.A15, J24.pulse
  N11: M1.B3, J20.pulse
  N12: M1.B4, J31.pulse
  N13: M1.B5, J28.pulse
  N14: M1.B6, J21.pulse
  N15: M1.B7, J23.pulse
  N16: M1.B8, J29.pulse
  N17: M1.B9, J19.pulse
  VCC: M1.5V, J2.Vcc, J3.Vcc, J4.Vcc, J5.Vcc, J6.Vcc, J7.Vcc, J8.Vcc, J9.Vcc, J10.Vcc, J11.Vcc, J12.Vcc, J13.Vcc, J14.Vcc, J15.Vcc, J16.Vcc, 5_volt_supply.VCC, J17.Vcc, J18.Vcc, J19.Vcc, J20.Vcc, J21.Vcc, J22.Vcc, J23.Vcc, J24.Vcc, J25.Vcc, J26.Vcc, J27.Vcc, J28.Vcc, J29.Vcc, J30.Vcc, J31.Vcc, Wafer_Servo.Vcc
  GND: M1.G, M1.GND, J2.gnd, J3.gnd, J4.gnd, J5.gnd, J6.gnd, J7.gnd, J8.gnd, J9.gnd, J10.gnd, J11.gnd, J12.gnd, J13.gnd, J14.gnd, J15.gnd, J16.gnd, 5_volt_supply.GND, J17.gnd, J18.gnd, J19.gnd, J20.gnd, J21.gnd, J22.gnd, J23.gnd, J24.gnd, J25.gnd, J26.gnd, J27.gnd, J28.gnd, J29.gnd, J30.gnd, J31.gnd, MIDI_Breakout.pin1, Wafer_Servo.gnd
  N18: M1.3.3V, MIDI_Breakout.pin2
  N19: M1.C13, J10.pulse
  N20: M1.C14, J8.pulse
  N21: M1.C15, J11.pulse
  N22: M1.A0, J7.pulse
  N23: M1.A1, J9.pulse
  N24: M1.A2, J2.pulse
  N25: M1.A3, J13.pulse
  N26: M1.A4, J12.pulse
  N27: M1.A5, J14.pulse
  N28: M1.A6, J16.pulse
  N29: M1.A7, J15.pulse
  N30: M1.B0, J6.pulse
  N31: M1.B1, J5.pulse
  N32: M1.B10, J4.pulse
  N33: M1.B11, J3.pulse
  N34: M1.CLK, Wafer_Servo.pulse

notes:
  Purple is RX
  Brown is TX
  We're out of GPIO pins, so we'll have to borrow one of the flashing pins (PA14) to drive the wafer servo. One unfortunate downside to this is that we now need to manually reset the board if we want to update the firmware.
